# Fritzing sketch Mintduino Game Circuit Diagram (saved by Fritzing 0.7.12b)
breadboards: 2

parts:
  S1 = Pushbutton [package="[THT]"]
  S2 = Pushbutton [package="[THT]"]
  LED1 = LED - 5mm [color="Red (633nm)" package="5 mm [THT]"]
  R2 = Resistor [tolerance=±5% resistance=100 package=THT]
  R3 = Resistor [tolerance=±5% resistance=100 package=THT]
  LED4 = green LED - 5mm
  LED5 = green LED - 5mm
  U1 = atmega168 [package=dip]
  S3 = Pushbutton [package="[THT]"]
  S4 = Pushbutton [package="[THT]"]
  LED6 = green LED - 5mm
  LED7 = green LED - 5mm
  R4 = Resistor [tolerance=±5% resistance=100 package=THT]
  R5 = Resistor [tolerance=±5% resistance=100 package=THT]
  R6 = Resistor [tolerance=±5% resistance=100 package=THT]

nets:
  N1: S1.Pin_1, S1.Pin_2, S2.Pin_1, S2.Pin_2, S3.Pin_3, S3.Pin_4, S4.Pin_3, S4.Pin_4
  N2: S1.Pin_3, S1.Pin_4, R2.Pin_1, LED5.cathode, U1.D3_(PWM)
  N3: S2.Pin_3, S2.Pin_4, R3.Pin_1, LED4.cathode, U1.D2
  N4: LED1.cathode, U1.D7
  N5: LED1.anode, R6.Pin_1
  N6: R2.Pin_0, R3.Pin_0, R6.Pin_0
  N7: LED4.anode, U1.D6_(PWM)
  N8: LED5.anode, U1.D5_(PWM)
  N9: U1.D10_(PWM), LED6.anode
  N10: U1.D11_(PWM), LED7.anode
  N11: U1.D12, S3.Pin_1, S3.Pin_2, LED6.cathode, R5.Pin_0
  N12: U1.D13, S4.Pin_1, S4.Pin_2, LED7.cathode, R4.Pin_0
  N13: R4.Pin_1, R5.Pin_1

notes:
  Mintduino
  Set to Arduino Duemilanove w/ ATmega328 to program.
  Player 1 LED = digitil pin 5
  Player 2 LED = digital pin 6
  Player 3 LED = digital pin 11
  Player 4 LED = digital pin 10
  Player 1 button = digital pin 4
  Player 2 button = digital pin 3
  Player 3 button = digital pin 13
  Player 4 button = digital pin 12
